// Logisim project proj_1.circ as structural Verilog: 4 circuits, main circuit main
module main (
);

  wire clock_1_out, dec_counter_1__0, dec_counter_1__1, dec_counter_1__2, dec_counter_1__3;

  Clock clock_1 (.out(clock_1_out));
  dec_counter dec_counter_1 (
    .Clock(clock_1_out), ._0(dec_counter_1__0), ._1(dec_counter_1__1), ._2(dec_counter_1__2),
    ._3(dec_counter_1__3));  // open: RESET
  _7_Segment_Display u_7_segment_display_1 ();  // open: g, f, a, b, e, d, c, dp
endmodule

module bonus (
);

  _7_Segment_Display u_7_segment_display_1 ();  // open: g, f, a, b, e, d, c, dp
  _7_Segment_Display u_7_segment_display_2 ();  // open: g, f, a, b, e, d, c, dp
endmodule

module dec_7seg_driver (
  input  in_1,
  input  in_2,
  input  in_3,
  input  in_4
);
endmodule

module dec_counter (
  input  Clock,
  output _0,
  output _1,
  output _2,
  output _3,
  output RESET
);

  wire and_2_out, and_3_out, and_4_out, and_5_out, and_6_out, and_7_out, and_8_out, D1_qn, D2_qn, D3_qn,
       D4_qn, or_1_out, or_2_out, or_3_out;

  and and_1 (RESET, _3, D2_qn, D3_qn, _0);
  and and_2 (and_2_out, _3, D4_qn);
  and and_3 (and_3_out, _2, _1, _0);
  and and_4 (and_4_out, _2, D3_qn);
  and and_5 (and_5_out, _2, D4_qn);
  and and_6 (and_6_out, D2_qn, _1, _0);
  and and_7 (and_7_out, _1, D4_qn);
  and and_8 (and_8_out, D1_qn, D3_qn, _0);
  or or_1 (or_1_out, and_2_out, and_3_out);
  or or_2 (or_2_out, and_4_out, and_5_out, and_6_out);
  or or_3 (or_3_out, and_7_out, and_8_out);
  D_Flip_Flop #(.trigger("falling")) D1 (.clk(Clock), .D(or_1_out), .Q(_3), .Qn(D1_qn));  // open: preset, en, reset
  D_Flip_Flop #(.trigger("falling")) D2 (.clk(Clock), .D(or_2_out), .Q(_2), .Qn(D2_qn));  // open: preset, en, reset
  D_Flip_Flop #(.trigger("falling")) D3 (.clk(Clock), .D(or_3_out), .Q(_1), .Qn(D3_qn));  // open: preset, en, reset
  D_Flip_Flop #(.trigger("falling")) D4 (.clk(Clock), .D(D4_qn), .Q(_0), .Qn(D4_qn));  // open: preset, en, reset
endmodule
